// Logisim project hw3-2.circ as structural Verilog: 18 circuits, main circuit main
module main (
);

  wire alu_8bit_basic_2_is_zero, alu_8bit_basic_2_overflow, clock, multiplexer_3_out, not_1_out;
  wire [7:0] alu_8bit_basic_1_main_output, alu_8bit_basic_2_main_output, multiplexer_1_out,
       multiplexer_2_out, multiplexer_4_out, multiplexer_5_out, my_register_file_1_rega,
       my_register_file_1_regb, PC_q, ram_1_dout;
  wire [27:0] rom_1_data;

  Clock clock_1 (.out(clock));
  Register PC (.D(multiplexer_1_out), .en(1'b1), .clk(clock), .Q(PC_q));  // open: clr
  ROM #(.dataWidth(28)) rom_1 (.addr(PC_q), .data(rom_1_data));
  Multiplexer #(.width(8)) multiplexer_1 (
    .in0(alu_8bit_basic_1_main_output), .in1(multiplexer_2_out), .out(multiplexer_1_out), .sel(rom_1_data[26]));
  ALU_8bit_basic alu_8bit_basic_1 (
    .A(8'h1), .B(PC_q), .opcode(4'b0010), .main_output(alu_8bit_basic_1_main_output));  // open: overflow, is_zero
  Multiplexer #(.width(8)) multiplexer_2 (
    .in0(alu_8bit_basic_1_main_output), .in1(rom_1_data[7:0]), .out(multiplexer_2_out),
    .sel(multiplexer_3_out));
  Multiplexer multiplexer_3 (
    .in0(alu_8bit_basic_2_is_zero), .in1(not_1_out), .out(multiplexer_3_out), .sel(rom_1_data[25]));
  Multiplexer #(.width(8)) multiplexer_4 (
    .in0(alu_8bit_basic_2_main_output), .in1(ram_1_dout), .out(multiplexer_4_out), .sel(rom_1_data[24]));
  not not_1 (not_1_out, alu_8bit_basic_2_is_zero);
  MY_REGISTER_FILE my_register_file_1 (
    .clock(clock), .write_en(rom_1_data[23]), .reg_w_sel(rom_1_data[16:14]), .reg_ra_sel(rom_1_data[13:11]),
    .reg_rb_sel(rom_1_data[10:8]), .Data(multiplexer_4_out), .regA(my_register_file_1_rega),
    .regB(my_register_file_1_regb));
  Multiplexer #(.width(8)) multiplexer_5 (
    .in0(my_register_file_1_regb), .in1(rom_1_data[7:0]), .out(multiplexer_5_out), .sel(rom_1_data[22]));
  ALU_8bit_basic alu_8bit_basic_2 (
    .A(my_register_file_1_rega), .B(multiplexer_5_out), .opcode(rom_1_data[20:17]),
    .main_output(alu_8bit_basic_2_main_output), .overflow(alu_8bit_basic_2_overflow),
    .is_zero(alu_8bit_basic_2_is_zero));
  RAM #(.asyncread("true"), .trigger("falling")) ram_1 (
    .addr(alu_8bit_basic_2_main_output), .we(rom_1_data[21]), .oe(rom_1_data[24]), .clk(clock),
    .din(my_register_file_1_regb), .dout(ram_1_dout));
  LED led_1 (.in(alu_8bit_basic_2_overflow));

  // Notes on the sheet:
  //   contents of rom_1 (hex, n*v repeats v):
  //   0 c45003 c48002 84ca00 8d1100 814a00 838a00 8fd300 98d300 640b01 1c51002 60c1a0d c4400d 40c2a0f
  //   c4800e 4000001
  //   rb
  //   ra
  //   rd
  //   ALU opcode
endmodule

module MY_1BIT_ADDER (
  input  a,
  input  b,
  input  c_in,
  output res,
  output c_out
);

  wire and_1_out, and_2_out, xor_1_out;

  xor xor_1 (xor_1_out, a, b);
  xor xor_2 (res, xor_1_out, c_in);
  and and_1 (and_1_out, xor_1_out, c_in);
  and and_2 (and_2_out, a, b);
  or or_1 (c_out, and_1_out, and_2_out);
endmodule

module MY_8BIT_ADDER (
  input  [7:0] in_1,
  input  [7:0] in_2,
  output [7:0] out_3
);

  wire my_1bit_adder_1_c_out, my_1bit_adder_2_c_out, my_1bit_adder_3_c_out, my_1bit_adder_4_c_out,
       my_1bit_adder_5_c_out, my_1bit_adder_6_c_out, my_1bit_adder_7_c_out, my_1bit_adder_8_c_out;

  MY_1BIT_ADDER my_1bit_adder_1 (
    .a(in_1[0]), .b(in_2[0]), .res(out_3[0]), .c_out(my_1bit_adder_1_c_out));  // open: c_in
  MY_1BIT_ADDER my_1bit_adder_2 (
    .a(in_1[1]), .b(in_2[1]), .c_in(my_1bit_adder_1_c_out), .res(out_3[1]), .c_out(my_1bit_adder_2_c_out));
  MY_1BIT_ADDER my_1bit_adder_3 (
    .a(in_1[2]), .b(in_2[2]), .c_in(my_1bit_adder_2_c_out), .res(out_3[2]), .c_out(my_1bit_adder_3_c_out));
  MY_1BIT_ADDER my_1bit_adder_4 (
    .a(in_1[3]), .b(in_2[3]), .c_in(my_1bit_adder_3_c_out), .res(out_3[3]), .c_out(my_1bit_adder_4_c_out));
  MY_1BIT_ADDER my_1bit_adder_5 (
    .a(in_1[4]), .b(in_2[4]), .c_in(my_1bit_adder_4_c_out), .res(out_3[4]), .c_out(my_1bit_adder_5_c_out));
  MY_1BIT_ADDER my_1bit_adder_6 (
    .a(in_1[5]), .b(in_2[5]), .c_in(my_1bit_adder_5_c_out), .res(out_3[5]), .c_out(my_1bit_adder_6_c_out));
  MY_1BIT_ADDER my_1bit_adder_7 (
    .a(in_1[6]), .b(in_2[6]), .c_in(my_1bit_adder_6_c_out), .res(out_3[6]), .c_out(my_1bit_adder_7_c_out));
  MY_1BIT_ADDER my_1bit_adder_8 (
    .a(in_1[7]), .b(in_2[7]), .c_in(my_1bit_adder_7_c_out), .res(out_3[7]), .c_out(my_1bit_adder_8_c_out));
endmodule

module ALU_basic (
  input  in_1,
  input  in_2,
  input  in_3,
  output out_4
);

  wire and_1_out, or_1_out;

  and and_1 (and_1_out, in_1, in_2);
  or or_1 (or_1_out, in_1, in_2);
  Multiplexer multiplexer_1 (.in0(and_1_out), .in1(or_1_out), .out(out_4), .sel(in_3));
endmodule

module ALU_basic_plus_addition (
  input  A,
  input  B,
  input  C_in,
  input  [1:0] op,
  output result,
  output c_out
);

  wire and_1_out, my_1bit_adder_1_res, or_1_out;

  and and_1 (and_1_out, A, B);
  or or_1 (or_1_out, A, B);
  MY_1BIT_ADDER my_1bit_adder_1 (.a(A), .b(B), .c_in(C_in), .res(my_1bit_adder_1_res), .c_out(c_out));
  Multiplexer #(.select(2)) multiplexer_1 (
    .in0(and_1_out), .in1(or_1_out), .in2(my_1bit_adder_1_res), .out(result), .sel(op));  // open: in3
endmodule

module ALU_4bit_basic (
  input  [3:0] A,
  input  [3:0] B,
  input  [1:0] op_code,
  output [3:0] Result,
  output C_out
);

  wire alu_basic_plus_addition_1_c_out, alu_basic_plus_addition_2_c_out, alu_basic_plus_addition_3_c_out;

  ALU_basic_plus_addition alu_basic_plus_addition_1 (
    .A(A[0]), .B(B[0]), .C_in(1'b0), .op(op_code), .result(Result[0]), .c_out(alu_basic_plus_addition_1_c_out));
  ALU_basic_plus_addition alu_basic_plus_addition_2 (
    .A(A[1]), .B(B[1]), .C_in(alu_basic_plus_addition_1_c_out), .op(op_code), .result(Result[1]),
    .c_out(alu_basic_plus_addition_2_c_out));
  ALU_basic_plus_addition alu_basic_plus_addition_3 (
    .A(A[2]), .B(B[2]), .C_in(alu_basic_plus_addition_2_c_out), .op(op_code), .result(Result[2]),
    .c_out(alu_basic_plus_addition_3_c_out));
  ALU_basic_plus_addition alu_basic_plus_addition_4 (
    .A(A[3]), .B(B[3]), .C_in(alu_basic_plus_addition_3_c_out), .op(op_code), .result(Result[3]),
    .c_out(C_out));
endmodule

module ALU_8bit_basic (
  input  [3:0] opcode,
  input  [7:0] A,
  input  [7:0] B,
  output is_zero,
  output [7:0] main_output,
  output overflow
);

  wire alu_1bit_1_c_out, alu_1bit_2_c_out, alu_1bit_3_c_out, alu_1bit_4_c_out, alu_1bit_5_c_out,
       alu_1bit_6_c_out, alu_1bit_7_c_out, alu_msb_1_slt, or_1_out;

  ALU_1bit alu_1bit_1 (
    .A_inv(opcode[3]), .B(B[0]), .B_inv(opcode[2]), .A(A[0]), .C_in(opcode[2]), .func(opcode[1:0]),
    .less(alu_msb_1_slt), .c_out(alu_1bit_1_c_out), .result(main_output[0]));
  ALU_1bit alu_1bit_2 (
    .A_inv(opcode[3]), .B(B[1]), .B_inv(opcode[2]), .A(A[1]), .C_in(alu_1bit_1_c_out), .func(opcode[1:0]),
    .less(1'b0), .c_out(alu_1bit_2_c_out), .result(main_output[1]));
  ALU_1bit alu_1bit_3 (
    .A_inv(opcode[3]), .B(B[2]), .B_inv(opcode[2]), .A(A[2]), .C_in(alu_1bit_2_c_out), .func(opcode[1:0]),
    .less(1'b0), .c_out(alu_1bit_3_c_out), .result(main_output[2]));
  ALU_1bit alu_1bit_4 (
    .A_inv(opcode[3]), .B(B[3]), .B_inv(opcode[2]), .A(A[3]), .C_in(alu_1bit_3_c_out), .func(opcode[1:0]),
    .less(1'b0), .c_out(alu_1bit_4_c_out), .result(main_output[3]));
  ALU_1bit alu_1bit_5 (
    .A_inv(opcode[3]), .B(B[4]), .B_inv(opcode[2]), .A(A[4]), .C_in(alu_1bit_4_c_out), .func(opcode[1:0]),
    .less(1'b0), .c_out(alu_1bit_5_c_out), .result(main_output[4]));
  ALU_1bit alu_1bit_6 (
    .A_inv(opcode[3]), .B(B[5]), .B_inv(opcode[2]), .A(A[5]), .C_in(alu_1bit_5_c_out), .func(opcode[1:0]),
    .less(1'b0), .c_out(alu_1bit_6_c_out), .result(main_output[5]));
  ALU_1bit alu_1bit_7 (
    .A_inv(opcode[3]), .B(B[6]), .B_inv(opcode[2]), .A(A[6]), .C_in(alu_1bit_6_c_out), .func(opcode[1:0]),
    .less(1'b0), .c_out(alu_1bit_7_c_out), .result(main_output[6]));
  ALU_MSB alu_msb_1 (
    .func(opcode[1:0]), .A_inv(opcode[3]), .B(B[7]), .B_inv(opcode[2]), .A(A[7]), .C_in(alu_1bit_7_c_out),
    .less(1'b0), .result(main_output[7]), .slt(alu_msb_1_slt), .overflow(overflow));
  or or_1 (or_1_out, main_output[0], main_output[1], main_output[2], main_output[3], main_output[4], main_output[5], main_output[6], main_output[7]);
  not not_1 (is_zero, or_1_out);
endmodule

module ALU_1bit (
  input  A,
  input  A_inv,
  input  B,
  input  less,
  input  B_inv,
  input  C_in,
  input  [1:0] func,
  output result,
  output c_out
);

  wire and_1_out, multiplexer_1_out, multiplexer_2_out, my_1bit_adder_1_res, not_1_out, not_2_out, or_1_out;

  not not_1 (not_1_out, A);
  not not_2 (not_2_out, B);
  Multiplexer multiplexer_1 (.in0(A), .in1(not_1_out), .out(multiplexer_1_out), .sel(A_inv));
  Multiplexer multiplexer_2 (.in0(B), .in1(not_2_out), .out(multiplexer_2_out), .sel(B_inv));
  and and_1 (and_1_out, multiplexer_1_out, multiplexer_2_out);
  or or_1 (or_1_out, multiplexer_1_out, multiplexer_2_out);
  MY_1BIT_ADDER my_1bit_adder_1 (
    .a(multiplexer_1_out), .b(multiplexer_2_out), .c_in(C_in), .res(my_1bit_adder_1_res), .c_out(c_out));
  Multiplexer #(.select(2)) multiplexer_3 (
    .in0(and_1_out), .in1(or_1_out), .in2(my_1bit_adder_1_res), .in3(less), .out(result), .sel(func));
endmodule

module ALU_MSB (
  input  A,
  input  A_inv,
  input  B,
  input  less,
  input  B_inv,
  input  C_in,
  input  [1:0] func,
  output result,
  output slt,
  output overflow
);

  wire and_1_out, multiplexer_1_out, multiplexer_2_out, my_1bit_adder_1_c_out, not_1_out, not_2_out, or_1_out;

  not not_1 (not_1_out, A);
  not not_2 (not_2_out, B);
  Multiplexer multiplexer_1 (.in0(A), .in1(not_1_out), .out(multiplexer_1_out), .sel(A_inv));
  Multiplexer multiplexer_2 (.in0(B), .in1(not_2_out), .out(multiplexer_2_out), .sel(B_inv));
  and and_1 (and_1_out, multiplexer_1_out, multiplexer_2_out);
  or or_1 (or_1_out, multiplexer_1_out, multiplexer_2_out);
  MY_1BIT_ADDER my_1bit_adder_1 (
    .a(multiplexer_1_out), .b(multiplexer_2_out), .c_in(C_in), .res(slt), .c_out(my_1bit_adder_1_c_out));
  Multiplexer #(.select(2)) multiplexer_3 (
    .in0(and_1_out), .in1(or_1_out), .in2(slt), .in3(less), .out(result), .sel(func));
  xor xor_1 (overflow, my_1bit_adder_1_c_out, C_in);
endmodule

module ALU_8bit_testing (
  input  [3:0] in_1,
  input  [7:0] in_2,
  input  [7:0] in_3,
  output [7:0] Result,
  output is_zero
);

  ALU_8bit_basic alu_8bit_basic_1 (
    .A(in_2), .B(in_3), .opcode(in_1), .main_output(Result), .is_zero(is_zero));  // open: overflow
endmodule

module MY_REGISTER_FILE (
  input  [7:0] Data,
  input  clock,
  input  write_en,
  input  [2:0] reg_w_sel,
  input  [2:0] reg_ra_sel,
  input  [2:0] reg_rb_sel,
  output [7:0] regA,
  output [7:0] regB
);

  wire demultiplexer_1_out1, demultiplexer_1_out2, demultiplexer_1_out3, demultiplexer_1_out4,
       demultiplexer_1_out5, demultiplexer_1_out6, demultiplexer_1_out7;
  wire [7:0] register_1_q, register_2_q, register_3_q, register_4_q, register_5_q, register_6_q, register_7_q;

  Demultiplexer #(.select(3)) demultiplexer_1 (
    .out1(demultiplexer_1_out1), .out2(demultiplexer_1_out2), .out3(demultiplexer_1_out3),
    .out4(demultiplexer_1_out4), .out5(demultiplexer_1_out5), .out6(demultiplexer_1_out6),
    .out7(demultiplexer_1_out7), .in(write_en), .sel(reg_w_sel));  // open: out0
  Register register_1 (.D(Data), .en(demultiplexer_1_out1), .clk(clock), .Q(register_1_q));  // open: clr
  Register register_2 (.D(Data), .en(demultiplexer_1_out2), .clk(clock), .Q(register_2_q));  // open: clr
  Register register_3 (.D(Data), .en(demultiplexer_1_out3), .clk(clock), .Q(register_3_q));  // open: clr
  Register register_4 (.D(Data), .en(demultiplexer_1_out4), .clk(clock), .Q(register_4_q));  // open: clr
  Register register_5 (.D(Data), .en(demultiplexer_1_out5), .clk(clock), .Q(register_5_q));  // open: clr
  Register register_6 (.D(Data), .en(demultiplexer_1_out6), .clk(clock), .Q(register_6_q));  // open: clr
  Register register_7 (.D(Data), .en(demultiplexer_1_out7), .clk(clock), .Q(register_7_q));  // open: clr
  Multiplexer #(.select(3), .width(8)) multiplexer_1 (
    .in0({8{1'b0}}), .in1(register_1_q), .in2(register_2_q), .in3(register_3_q), .in4(register_4_q),
    .in5(register_5_q), .in6(register_6_q), .in7(register_7_q), .out(regA), .sel(reg_ra_sel));
  Multiplexer #(.select(3), .width(8)) multiplexer_2 (
    .in0({8{1'b0}}), .in1(register_1_q), .in2(register_2_q), .in3(register_3_q), .in4(register_4_q),
    .in5(register_5_q), .in6(register_6_q), .in7(register_7_q), .out(regB), .sel(reg_rb_sel));

  // Other names for the same wires on the sheet: ra_sel[2:0] = reg_ra_sel; rb_sel[2:0] = reg_rb_sel
endmodule

module reg_file_testing (
  input  [2:0] in_1,
  input  [7:0] in_2,
  input  [2:0] in_3,
  input  [2:0] in_4,
  input  in_5,
  output [7:0] out_6,
  output [7:0] out_7
);

  wire clock_1_out;

  Clock clock_1 (.out(clock_1_out));
  MY_REGISTER_FILE my_register_file_1 (
    .clock(clock_1_out), .write_en(in_5), .reg_w_sel(in_3), .reg_ra_sel(in_1), .reg_rb_sel(in_4),
    .Data(in_2), .regA(out_6), .regB(out_7));
endmodule

module LED_DISPLAYER (
  input  [3:0] in_1
);

  LED led_1 (.in(in_1[3]));
  LED led_2 (.in(in_1[2]));
  LED led_3 (.in(in_1[1]));
  LED led_4 (.in(in_1[0]));
endmodule

module LED_DECODER (
  input  [1:0] in_1
);

  wire and_1_out, and_2_out, and_3_out, and_4_out, not_1_out, not_2_out, not_3_out, not_4_out;

  not not_1 (not_1_out, in_1[0]);
  not not_2 (not_2_out, in_1[1]);
  not not_3 (not_3_out, in_1[0]);
  not not_4 (not_4_out, in_1[1]);
  and and_1 (and_1_out, in_1[0], in_1[1]);
  and and_2 (and_2_out, not_1_out, in_1[1]);
  and and_3 (and_3_out, in_1[0], not_2_out);
  and and_4 (and_4_out, not_3_out, not_4_out);
  LED three (.in(and_1_out));
  LED two (.in(and_2_out));
  LED one (.in(and_3_out));
  LED zero (.in(and_4_out));
endmodule

module MULTIPLEXER_2bit (
  input  [7:0] A_00,
  input  [7:0] B_01,
  input  [7:0] C_10,
  input  [7:0] D_11,
  input  [1:0] SEL,
  output [7:0] out_6
);

  wire not_1_out, not_2_out, not_3_out, not_4_out;
  wire [7:0] and_1_out, and_2_out, and_3_out, and_4_out, and_5_out, and_6_out, and_7_out, and_8_out,
       bit_extender_1_out, bit_extender_2_out, bit_extender_3_out, bit_extender_4_out, bit_extender_5_out,
       bit_extender_6_out, bit_extender_7_out, bit_extender_8_out, or_1_out, or_2_out;

  not not_1 (not_1_out, SEL[1]);
  not not_2 (not_2_out, SEL[0]);
  not not_3 (not_3_out, SEL[1]);
  not not_4 (not_4_out, SEL[0]);
  assign bit_extender_1_out = {{7{not_1_out}}, not_1_out};  // Bit_Extender bit_extender_1
  assign bit_extender_2_out = {{7{not_2_out}}, not_2_out};  // Bit_Extender bit_extender_2
  assign bit_extender_3_out = {{7{not_3_out}}, not_3_out};  // Bit_Extender bit_extender_3
  assign bit_extender_4_out = {{7{SEL[0]}}, SEL[0]};  // Bit_Extender bit_extender_4
  assign bit_extender_5_out = {{7{SEL[1]}}, SEL[1]};  // Bit_Extender bit_extender_5
  assign bit_extender_6_out = {{7{not_4_out}}, not_4_out};  // Bit_Extender bit_extender_6
  assign bit_extender_7_out = {{7{SEL[1]}}, SEL[1]};  // Bit_Extender bit_extender_7
  assign bit_extender_8_out = {{7{SEL[0]}}, SEL[0]};  // Bit_Extender bit_extender_8
  assign and_1_out = bit_extender_1_out & bit_extender_2_out;  // AND_Gate and_1, 8 bits wide
  assign and_2_out = bit_extender_3_out & bit_extender_4_out;  // AND_Gate and_2, 8 bits wide
  assign and_3_out = bit_extender_5_out & bit_extender_6_out;  // AND_Gate and_3, 8 bits wide
  assign and_4_out = bit_extender_7_out & bit_extender_8_out;  // AND_Gate and_4, 8 bits wide
  assign and_5_out = A_00 & and_1_out;  // AND_Gate and_5, 8 bits wide
  assign and_6_out = B_01 & and_2_out;  // AND_Gate and_6, 8 bits wide
  assign and_7_out = C_10 & and_3_out;  // AND_Gate and_7, 8 bits wide
  assign and_8_out = D_11 & and_4_out;  // AND_Gate and_8, 8 bits wide
  assign or_1_out = and_5_out | and_6_out;  // OR_Gate or_1, 8 bits wide
  assign or_2_out = and_7_out | and_8_out;  // OR_Gate or_2, 8 bits wide
  assign out_6 = or_1_out | or_2_out;  // OR_Gate or_3, 8 bits wide
endmodule

module DEMULTIPLEXER_2bit (
  input  [7:0] I,
  input  [1:0] SEL,
  output [7:0] A,
  output [7:0] B,
  output [7:0] C,
  output [7:0] D
);

  wire [7:0] and_1_out, and_2_out, and_3_out, and_4_out, bit_extender_1_out, bit_extender_2_out, not_1_out,
       not_2_out, not_3_out, not_4_out;

  assign bit_extender_1_out = {{7{SEL[0]}}, SEL[0]};  // Bit_Extender bit_extender_1
  assign bit_extender_2_out = {{7{SEL[1]}}, SEL[1]};  // Bit_Extender bit_extender_2
  assign not_1_out = ~bit_extender_1_out;  // NOT_Gate not_1, 8 bits wide
  assign not_2_out = ~bit_extender_2_out;  // NOT_Gate not_2, 8 bits wide
  assign not_3_out = ~bit_extender_2_out;  // NOT_Gate not_3, 8 bits wide
  assign not_4_out = ~bit_extender_1_out;  // NOT_Gate not_4, 8 bits wide
  assign and_1_out = not_1_out & not_2_out;  // AND_Gate and_1, 8 bits wide
  assign and_2_out = bit_extender_1_out & not_3_out;  // AND_Gate and_2, 8 bits wide
  assign and_3_out = not_4_out & bit_extender_2_out;  // AND_Gate and_3, 8 bits wide
  assign and_4_out = bit_extender_1_out & bit_extender_2_out;  // AND_Gate and_4, 8 bits wide
  assign A = I & and_1_out;  // AND_Gate and_5, 8 bits wide
  assign B = I & and_2_out;  // AND_Gate and_6, 8 bits wide
  assign C = I & and_3_out;  // AND_Gate and_7, 8 bits wide
  assign D = I & and_4_out;  // AND_Gate and_8, 8 bits wide
endmodule

module EXTENDER (
  input  in_1,
  output [7:0] out_2
);

  and and_1 (out_2[0], 1'b1, in_1);
  and and_2 (out_2[1], 1'b1, in_1);
  and and_3 (out_2[2], 1'b1, in_1);
  and and_4 (out_2[3], 1'b1, in_1);
  and and_5 (out_2[4], 1'b1, in_1);
  and and_6 (out_2[5], 1'b1, in_1);
  and and_7 (out_2[6], 1'b1, in_1);
  and and_8 (out_2[7], 1'b1, in_1);
endmodule

module PROGRAM_COUNTER (
  output [7:0] out_1
);

  wire alu_8bit_basic_1_overflow, clock_1_out, Reset_out;
  wire [7:0] alu_8bit_basic_1_main_output, multiplexer_1_out, PC_q;

  Clock clock_1 (.out(clock_1_out));
  Register PC (.D(multiplexer_1_out), .en(1'b1), .clk(clock_1_out), .Q(PC_q));  // open: clr
  Button Reset (.out(Reset_out));
  Multiplexer #(.width(8)) multiplexer_1 (
    .in0(alu_8bit_basic_1_main_output), .in1({8{1'b0}}), .out(multiplexer_1_out), .sel(Reset_out));
  ALU_8bit_basic alu_8bit_basic_1 (
    .A(8'h1), .B(PC_q), .opcode(4'b0010), .main_output(alu_8bit_basic_1_main_output),
    .overflow(alu_8bit_basic_1_overflow));  // open: is_zero
  LED led_1 (.in(alu_8bit_basic_1_overflow));
  ROM rom_1 (.addr(PC_q), .data(out_1));
endmodule
